# Fritzing sketch robot (saved by Fritzing 0.9.3b)
breadboards: 1

parts:
  L1 = Solenoid
  L2 = Solenoid
  L3 = Solenoid
  L4 = Solenoid
  Part1 = Arduino Pro Mini v13
  Q1 = NPN-Transistor [package="TO92 [THT]"]
  R1 = Photocell (LDR) [package=THT]
  LED1 = LED - 5mm [color="Red (633nm)" package="5 mm [THT]"]
  R2 = Resistor [tolerance=±5% resistance=220 package=THT]
  R3 = Resistor [tolerance=±5% resistance=10k package=THT]
  VCC1 = Battery block 9V

nets:
  N1: L1.pin1, L2.pin1, L3.pin1, L4.pin1, Part1.RAW, VCC1.+
  N2: L1.pin2, L2.pin2, L3.pin2, L4.pin2, Q1.C
  N3: Part1.VCC, LED1.anode, R3.Pin_1
  N4: Part1.GND, Q1.E, R1.pin_1, R2.Pin_1, VCC1.-
  N5: Part1.D10_PWM/SS, Q1.B
  N6: Part1.D2, R1.pin_0, R3.Pin_0
  N7: LED1.cathode, R2.Pin_0
